# Fritzing sketch toprak (saved by Fritzing 0.9.3b)
breadboards: 1

parts:
  부품3 = FC-28 Soil Hygrometer Module - Probe
  부품4 = FC-28 Soil Hygrometer Module
  WATER_PUMP2 = water pump/motor  # not connected
  C1 = Electrolytic Capacitor [capacitance=100µF package="200 mil [THT, electrolytic]"]
  L298N2 = L298N DC motor driver
  LED1 = LED - 3mm [color="Green (570nm)" package="3 mm [THT]"]
  LED2 = smd LED [color="Red (633nm)" package="1206 [SMD]"]
  T2 = LM35 Temperature Sensor [package="TO92 [THT]"]
  BT1 = Bluetooth HC-06u [package=THT]
  Parça2 = Arduino Uno (Rev3)

nets:
  N1: 부품3.POS, 부품4.POS
  N2: 부품3.NEG, 부품4.NEG
  VCC: 부품4.VCC, T2.+Vs, BT1.VCC, Parça2.3V3
  GND: 부품4.GND, C1.-, L298N2.GND, LED1.anode, LED2.anode, T2.GND, BT1.GND, Parça2.GND
  N3: 부품4.AO, Parça2.A0
  N4: C1.+, T2.Vout, Parça2.A1
  12V: L298N2.12V, Parça2.VIN
  5V: L298N2.5V, Parça2.5V
  N5: L298N2.IN1, Parça2.D2
  N6: L298N2.IN2, Parça2.D3_PWM
  N7: LED1.cathode, Parça2.D5_PWM
  N8: LED2.cathode, Parça2.D6_PWM

custom parts:
  FC-28 Soil Hygrometer Module - Probe: The FC-28 is a soil hygrometer module that uses the Texas Instruments LM393 comparator chip to provide an analog measurement of soil humidity.
  FC-28 Soil Hygrometer Module: The FC-28 is a soil hygrometer module that uses the Texas Instruments LM393 comparator chip to provide an analog measurement of soil humidity. The digital output is high when soil moisture is over a certain threshold, as determined by adjusting the potentiometer.
  water pump/motor: WATER PUMP BY ARDUBLOCKTR
  L298N DC motor driver: 2x DC motor driver with 78M05 positive voltage regulator (7..35 V) L298N: max 46 V, 2 A Set 5 V Enable jumper to enable 5 V regultor (needed for the L298N) and +5 V output at screw terminal or supply external +5 V at screw terminal Set ENA and/or ENB to +5 V to enable motor permanently or supply ENA and/or ENB with PWM signal IN1 and IN2 set rotation directory for motor A (OUT1/OUT2) IN2 and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
  Bluetooth HC-06u: Bluetooth HC-06 - face up, pins down 16.5mm x 37.5mm PCB
